// Logisim project CSE_332_Lab_Assignment_NO_02.circ as structural Verilog: 2 circuits, main circuit main
module main (
  input  ENABLE,
  input  [31:0] Ainput,
  output [31:0] Yout
);

  wire and_1_out, CLK_out;

  D_Flip_Flop d_ff_1 (.D(Ainput[31]), .clk(and_1_out), .Q(Yout[31]));  // open: Qn, preset, reset
  D_Flip_Flop d_ff_2 (.D(Ainput[30]), .clk(and_1_out), .Q(Yout[30]));  // open: Qn, preset, reset
  Clock CLK (.out(CLK_out));
  and and_1 (and_1_out, CLK_out, ENABLE);
  D_Flip_Flop d_ff_3 (.D(Ainput[29]), .clk(and_1_out), .Q(Yout[29]));  // open: Qn, preset, reset
  D_Flip_Flop d_ff_4 (.D(Ainput[28]), .clk(and_1_out), .Q(Yout[28]));  // open: Qn, preset, reset
  D_Flip_Flop d_ff_5 (.D(Ainput[27]), .clk(and_1_out), .Q(Yout[27]));  // open: Qn, preset, reset
  D_Flip_Flop d_ff_6 (.D(Ainput[26]), .clk(and_1_out), .Q(Yout[26]));  // open: Qn, preset, reset
  D_Flip_Flop d_ff_7 (.D(Ainput[25]), .clk(and_1_out), .Q(Yout[25]));  // open: Qn, preset, reset
  D_Flip_Flop d_ff_8 (.D(Ainput[24]), .clk(and_1_out), .Q(Yout[24]));  // open: Qn, preset, reset
  D_Flip_Flop d_ff_9 (.D(Ainput[23]), .clk(and_1_out), .Q(Yout[23]));  // open: Qn, preset, reset
  D_Flip_Flop d_ff_10 (.D(Ainput[22]), .clk(and_1_out), .Q(Yout[22]));  // open: Qn, preset, reset
  D_Flip_Flop d_ff_11 (.D(Ainput[21]), .clk(and_1_out), .Q(Yout[21]));  // open: Qn, preset, reset
  D_Flip_Flop d_ff_12 (.D(Ainput[20]), .clk(and_1_out), .Q(Yout[20]));  // open: Qn, preset, reset
  D_Flip_Flop d_ff_13 (.D(Ainput[19]), .clk(and_1_out), .Q(Yout[19]));  // open: Qn, preset, reset
  D_Flip_Flop d_ff_14 (.D(Ainput[18]), .clk(and_1_out), .Q(Yout[18]));  // open: Qn, preset, reset
  D_Flip_Flop d_ff_15 (.D(Ainput[17]), .clk(and_1_out), .Q(Yout[17]));  // open: Qn, preset, reset
  D_Flip_Flop d_ff_16 (.D(Ainput[16]), .clk(and_1_out), .Q(Yout[16]));  // open: Qn, preset, reset
  D_Flip_Flop d_ff_17 (.D(Ainput[15]), .clk(and_1_out), .Q(Yout[15]));  // open: Qn, preset, reset
  D_Flip_Flop d_ff_18 (.D(Ainput[14]), .clk(and_1_out), .Q(Yout[14]));  // open: Qn, preset, reset
  D_Flip_Flop d_ff_19 (.D(Ainput[13]), .clk(and_1_out), .Q(Yout[13]));  // open: Qn, preset, reset
  D_Flip_Flop d_ff_20 (.D(Ainput[12]), .clk(and_1_out), .Q(Yout[12]));  // open: Qn, preset, reset
  D_Flip_Flop d_ff_21 (.D(Ainput[11]), .clk(and_1_out), .Q(Yout[11]));  // open: Qn, preset, reset
  D_Flip_Flop d_ff_22 (.D(Ainput[10]), .clk(and_1_out), .Q(Yout[10]));  // open: Qn, preset, reset
  D_Flip_Flop d_ff_23 (.D(Ainput[9]), .clk(and_1_out), .Q(Yout[9]));  // open: Qn, preset, reset
  D_Flip_Flop d_ff_24 (.D(Ainput[8]), .clk(and_1_out), .Q(Yout[8]));  // open: Qn, preset, reset
  D_Flip_Flop d_ff_25 (.D(Ainput[7]), .clk(and_1_out), .Q(Yout[7]));  // open: Qn, preset, reset
  D_Flip_Flop d_ff_26 (.D(Ainput[6]), .clk(and_1_out), .Q(Yout[6]));  // open: Qn, preset, reset
  D_Flip_Flop d_ff_27 (.D(Ainput[5]), .clk(and_1_out), .Q(Yout[5]));  // open: Qn, preset, reset
  D_Flip_Flop d_ff_28 (.D(Ainput[4]), .clk(and_1_out), .Q(Yout[4]));  // open: Qn, preset, reset
  D_Flip_Flop d_ff_29 (.D(Ainput[3]), .clk(and_1_out), .Q(Yout[3]));  // open: Qn, preset, reset
  D_Flip_Flop d_ff_30 (.D(Ainput[2]), .clk(and_1_out), .Q(Yout[2]));  // open: Qn, preset, reset
  D_Flip_Flop d_ff_31 (.D(Ainput[1]), .clk(and_1_out), .Q(Yout[1]));  // open: Qn, preset, reset
  D_Flip_Flop d_ff_32 (.D(Ainput[0]), .clk(and_1_out), .Q(Yout[0]));  // open: Qn, preset, reset
endmodule

module kk (
);

  main main_1 ();  // open: ENABLE, Ainput, Yout
endmodule
